// Logisim project alu.circ as structural Verilog: 1 circuit, main circuit alu
module alu (
  input  [31:0] A,
  input  [31:0] B,
  input  [3:0] ALUSel,
  output [31:0] Result
);

  wire bitselector_1_out, bitselector_2_out, bitselector_3_out, bitselector_4_out, bitselector_5_out,
       bitselector_6_out, comparator_1_eq, comparator_2_eq, xor_2_out;
  wire [4:0] bitselector_7_out, bitselector_8_out, bitselector_9_out;
  wire [5:0] bitadder_1_out, bitadder_2_out;
  wire [31:0] add_result, adder_1_out, adder_2_out, adder_4_out, adder_5_out, and_result, bit_extender_1_out,
       bit_extender_2_out, bit_extender_3_out, bit_extender_4_out, cnto_result, div_result, divider_1_out,
       divider_3_rem, divu_result, mulh_result, mulhu_result, mult_result, multiplexer_2_out,
       multiplexer_3_out, multiplier_1_cout, multiplier_3_out, multiplier_4_out, not_1_out, not_2_out,
       not_3_out, or_result, remu_result, sll_result, slt_result, sra_result, srl_result, sub_result,
       xor_result;

  Multiplexer #(.select(4), .width(32), .enable("false")) multiplexer_1 (
    .in0(add_result), .in1(or_result), .in2(xor_result), .in3(and_result), .in4(sub_result),
    .in5(mult_result), .in6(mulhu_result), .in7(mulh_result), .in8(divu_result), .in9(div_result),
    .in10(remu_result), .in11(srl_result), .in12(sra_result), .in13(slt_result), .in14(sll_result),
    .in15(cnto_result), .out(Result), .sel(ALUSel));
  assign not_1_out = ~A;  // NOT_Gate not_1, 32 bits wide
  assign not_2_out = ~B;  // NOT_Gate not_2, 32 bits wide
  BitSelector #(.width(32)) bitselector_1 (.in(A), .out(bitselector_1_out), .sel({5{1'b1}}));
  BitSelector #(.width(32)) bitselector_2 (.in(B), .out(bitselector_2_out), .sel({5{1'b1}}));
  Adder #(.width(32)) adder_1 (.a(not_1_out), .b(32'h1), .out(adder_1_out));  // open: cin, cout
  BitSelector #(.width(32)) bitselector_3 (.in(A), .out(bitselector_3_out), .sel({5{1'b1}}));
  Adder #(.width(32)) adder_2 (.a(not_2_out), .b(32'h1), .out(adder_2_out));  // open: cin, cout
  BitSelector #(.width(32)) bitselector_4 (.in(B), .out(bitselector_4_out), .sel({5{1'b1}}));
  assign add_result = A & B;  // AND_Gate and_1, 32 bits wide
  assign or_result = A | B;  // OR_Gate or_1, 32 bits wide
  assign xor_result = A ^ B;  // XOR_Gate xor_1, 32 bits wide
  Adder #(.width(32)) adder_3 (.a(A), .b(B), .out(and_result));  // open: cin, cout
  Subtractor #(.width(32)) subtractor_1 (.a(A), .b(B), .out(sub_result));  // open: bin, bout
  Multiplier #(.width(32)) multiplier_1 (.a(A), .b(B), .out(mult_result), .cout(multiplier_1_cout));  // open: cin
  Multiplier #(.width(32)) multiplier_2 (.a(A), .b(B), .cout(mulhu_result));  // open: out, cin
  assign bit_extender_1_out = {{31{bitselector_1_out}}, bitselector_1_out};  // Bit_Extender bit_extender_1
  assign bit_extender_2_out = {{31{bitselector_2_out}}, bitselector_2_out};  // Bit_Extender bit_extender_2
  Multiplexer #(.width(32), .enable("false")) multiplexer_2 (
    .in0(A), .in1(adder_1_out), .out(multiplexer_2_out), .sel(bitselector_3_out));
  Multiplexer #(.width(32), .enable("false")) multiplexer_3 (
    .in0(B), .in1(adder_2_out), .out(multiplexer_3_out), .sel(bitselector_4_out));
  Multiplier #(.width(32)) multiplier_3 (.a(bit_extender_1_out), .b(B), .out(multiplier_3_out));  // open: cin, cout
  Multiplier #(.width(32)) multiplier_4 (.a(A), .b(bit_extender_2_out), .out(multiplier_4_out));  // open: cin, cout
  Divider #(.width(32)) divider_1 (
    .a(multiplexer_2_out), .b(multiplexer_3_out), .out(divider_1_out));  // open: upper, rem
  Adder #(.width(32)) adder_4 (.a(multiplier_3_out), .b(multiplier_4_out), .out(adder_4_out));  // open: cin, cout
  assign not_3_out = ~divider_1_out;  // NOT_Gate not_3, 32 bits wide
  BitSelector #(.width(32)) bitselector_5 (.in(A), .out(bitselector_5_out), .sel({5{1'b1}}));
  BitSelector #(.width(32)) bitselector_6 (.in(B), .out(bitselector_6_out), .sel({5{1'b1}}));
  BitSelector #(.width(32), .group(5)) bitselector_7 (.in(B), .out(bitselector_7_out), .sel(3'b000));
  BitSelector #(.width(32), .group(5)) bitselector_8 (.in(B), .out(bitselector_8_out), .sel(3'b000));
  BitSelector #(.width(32), .group(5)) bitselector_9 (.in(B), .out(bitselector_9_out), .sel(3'b000));
  BitAdder #(.width(32)) bitadder_1 (.in0(A), .out(bitadder_1_out));
  BitAdder #(.width(32)) bitadder_2 (.in0(B), .out(bitadder_2_out));
  Adder #(.width(32)) adder_5 (.a(not_3_out), .b(32'h1), .out(adder_5_out));  // open: cin, cout
  xor xor_2 (xor_2_out, bitselector_5_out, bitselector_6_out);
  Divider #(.width(32)) divider_2 (.a(A), .b(B), .out(divu_result));  // open: upper, rem
  Comparator #(.width(32)) comparator_1 (.a({32{1'b0}}), .b(B), .eq(comparator_1_eq));  // open: gt, lt
  Shifter #(.width(32), .shift("lr")) shifter_1 (.in(A), .\dist (bitselector_7_out), .out(srl_result));
  Shifter #(.width(32), .shift("ar")) shifter_2 (.in(A), .\dist (bitselector_8_out), .out(sra_result));
  Comparator #(.width(32)) comparator_2 (.a(A), .b(B), .eq(comparator_2_eq));  // open: gt, lt
  Shifter #(.width(32)) shifter_3 (.in(A), .\dist (bitselector_9_out), .out(sll_result));
  assign bit_extender_3_out = {{26{1'b0}}, bitadder_1_out};  // Bit_Extender bit_extender_3
  assign bit_extender_4_out = {{26{1'b0}}, bitadder_2_out};  // Bit_Extender bit_extender_4
  Adder #(.width(32)) adder_6 (.a(adder_4_out), .b(mulhu_result), .out(mulh_result));  // open: cin, cout
  Multiplexer #(.width(32), .enable("false")) multiplexer_4 (
    .in1(adder_5_out), .out(div_result), .sel(xor_2_out));  // open: in0
  Divider #(.width(32)) divider_3 (.a(A), .b(B), .rem(divider_3_rem));  // open: out, upper
  assign slt_result = {{31{1'b0}}, comparator_2_eq};  // Bit_Extender bit_extender_5
  Adder #(.width(32)) adder_7 (.a(bit_extender_3_out), .b(bit_extender_4_out), .out(cnto_result));  // open: cin, cout
  Multiplexer #(.width(32), .enable("false")) multiplexer_5 (
    .in0(divider_3_rem), .in1(A), .out(remu_result), .sel(comparator_1_eq));

  // Notes on the sheet:
  //   INPUTS to your circuit
  //   DON'T CHANGE THE LOCATIONS OF THE INPUTS AND OUTPUTS!
  //   OUTPUT from your circuit
endmodule
